# Fritzing sketch Diagrama de conexion (saved by Fritzing 0.9.3b)

parts:
  Mod1 = Raspberry Pi 4B
  Cámara = Rasberry Pi NIOR Camera [chip_label=IC package="DIP (Dual Inline) [THT]"]  # not connected
  hc-sr1 = hc-sr04  # not connected
  Servo = Basic Servo
  M1 = DC Motor
  Motores = DC Motor
  Pilas = Battery Holders [package=battery-aa]
  BAT2 = Battery Holders [package=battery-aa]
  BAT3 = Battery Holders [package=battery-aa]
  BAT4 = Battery Holders [package=battery-aa]
  L298N = H-Bridge with L298N
  LED1 = LED - 5mm [color="Red (633nm)" package="5 mm [THT]"]  # not connected
  LED2 = LED - 5mm [color="Red (633nm)" package="5 mm [THT]"]  # not connected
  LED3 = LED - 5mm [color="Orange (605nm)" package="5 mm [THT]"]  # not connected
  LED4 = LED - 5mm [color="Orange (605nm)" package="5 mm [THT]"]  # not connected
  LED5 = LED - 5mm [color="White (4500K)" package="5 mm [THT]"]  # not connected
  LED6 = LED - 5mm [color="White (4500K)" package="5 mm [THT]"]  # not connected
  R1 = Resistor [tolerance=±5% resistance=1k package=THT]  # not connected
  R2 = Resistor [tolerance=±5% resistance=1k package=THT]  # not connected
  R3 = Resistor [tolerance=±5% resistance=1k package=THT]  # not connected
  R4 = Resistor [tolerance=±5% resistance=1k package=THT]  # not connected
  R5 = Resistor [tolerance=±5% resistance=1k package=THT]  # not connected
  R6 = Resistor [tolerance=±5% resistance=1k package=THT]  # not connected
  S3 = SWITCH-MOMENTARY-2 [package=reed_switch_pth]  # not connected
  GY1 = MPU-6050 Board GY-521 [form="♀ (female)" package=THT]  # not connected
  BMS = 2S-BMS
  Componente1 = TXB0108 8-channel Bi-directional Logic Level Converter  # not connected
  Voltimetro = MH-DL18S [package=THT]
  Step_down = LM2596 step down module
  Interruptor = Toggle Switch [package=THT]
  IC1 = Rasberry Pi NIOR Camera [chip_label=IC package="DIP (Dual Inline) [THT]"]  # not connected
  LED7 = LED - 5mm [color="Orange (605nm)" package="5 mm [THT]"]  # not connected
  LED8 = LED - 5mm [color="Orange (605nm)" package="5 mm [THT]"]  # not connected
  R7 = Resistor [tolerance=±5% resistance=1k package=THT]  # not connected
  R8 = Resistor [tolerance=±5% resistance=1k package=THT]  # not connected

nets:
  5V: Mod1.5V, Servo.vcc, L298N.5V
  GND: Mod1.GND, Servo.gnd, L298N.GND
  N1: Mod1.GPIO25, Servo.pulse
  N2: Mod1.GPIO6, L298N.ENB
  N3: Mod1.GPIO12, L298N.IN4
  N4: Mod1.GPIO13, L298N.IN3
  N5: M1.pin_1, Motores.pin_1, L298N.M2-01
  N6: M1.pin_2, Motores.pin_2, L298N.M2-02
  N7: Pilas.-, BAT4.-, Voltimetro.Battery_-
  N8: Pilas.+, BAT2.-, BAT3.-, BAT4.+, BMS.pin3#3
  N9: BAT2.+, BAT3.+, Interruptor.L2
  N10: BMS.pin1, Interruptor.COM
  N11: BMS.pin2, Voltimetro.Battery_+
  N12: BMS.pin3#2, Step_down.IN-, Step_down.OUT-
  N13: BMS.pin3#4, Step_down.IN+

custom parts:
  Rasberry Pi NIOR Camera: Camera
  H-Bridge with L298N: h-bridge
  MPU-6050 Board GY-521: Acelerometro y Giroscopio MPU-6050 Board GY-521
  2S-BMS: 2S-BMS LIPO battery charger / protection unit. Note pcb does not match the board as it will likely connect with wires, so pcb is 5 pads suitable for .1in header pins.
  TXB0108 8-channel Bi-directional Logic Level Converter: Because the Arduino (and Basic Stamp) are 5V devices, and most modern sensors, displays, flash cards and modes are 3.3V-only, many makers find that they need to perform level shifting/conversion to protect the 3.3V device from 5V. Although one can use resistors to make a divider, for high speed transfers, the resistors can add a lot of slew and cause havoc that is tough to debug. For that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
  MH-DL18S: 1S 2S 3S 4S Single 3.7V Lithium battery capacity LED indicator module.
  LM2596 step down module: LM2596 DC-DC step down power supply module 3 A.
